# Fritzing sketch sdcardWavPlayer (saved by Fritzing 0.9.3b)
breadboards: 1

parts:
  Part1 = Arduino Uno (Rev3)
  microSD1 = MicroSD Card Module
  SP1 = SPEAKER [package=pcb_mount_speaker]
  R1 = Resistor [tolerance=±5% resistance=47 package="0805 [SMD]"]
  S1 = Pushbutton [package="[SMD]"]
  S2 = Pushbutton [package="[SMD]"]
  R2 = Resistor [tolerance=±5% resistance=10k package="0805 [SMD]"]
  R3 = Resistor [tolerance=±5% resistance=10k package="0805 [SMD]"]

nets:
  N1: Part1.D9_PWM, SP1.-
  N2: Part1.D10_PWM/SS, microSD1.CS
  N3: Part1.D11_PWM/MOSI, microSD1.MOSI
  N4: Part1.D12/MISO, microSD1.MISO
  N5: Part1.D13/SCK, microSD1.SCK
  N6: Part1.D2, S2.Pin_1, S2.Pin_2, R3.Pin_0
  N7: Part1.D3_PWM, S1.Pin_1, S1.Pin_2, R2.Pin_0
  5V: Part1.5V, microSD1.VCC
  GND: Part1.GND, microSD1.GND, R1.Pin_1, R2.Pin_1, R3.Pin_1
  N8: SP1.+, R1.Pin_0
  N9: S1.Pin_3, S1.Pin_4
  N10: S2.Pin_3, S2.Pin_4

notes:
  Left button Play/Pause
  Right button next song
  SCK 13
  MISO 12
  MOSI 11
  CS 10
